# Fritzing sketch timelock (saved by Fritzing 0.9.0b)
circuit board: 5.34055cm x 5.45755cm
breadboards: 1

parts:
  R2 = Resistor [tolerance=±5% resistance=330 package=THT]
  Base_Resistor = Resistor [tolerance=±5% resistance=330 package=THT]
  R4 = Resistor [tolerance=±5% resistance=330 package=THT]
  LED_Resistor = Resistor [tolerance=±5% resistance=330 package=THT]
  DCF_Pullup = Resistor [tolerance=±5% resistance=10k package=THT]
  SG90 = Basic Servo
  p2n2222ag = NPN-Transistor [package="TO92 [THT]"]
  Part1 = Arduino Uno (Rev3)
  DCF77_Receiver_-_Conrad_1 = DCF77 641138
  LED1 = RGB LED (com. cathode, rgb) [package="5 mm [THT]"]

nets:
  N1: R2.Pin_0, LED1.green_anode
  N2: R2.Pin_1, Part1.D5_PWM
  N3: Base_Resistor.Pin_0, p2n2222ag.B
  N4: Base_Resistor.Pin_1, Part1.D8
  N5: R4.Pin_0, LED1.blue_anode
  N6: R4.Pin_1, Part1.D3_PWM
  N7: LED_Resistor.Pin_0, LED1.red_anode
  N8: LED_Resistor.Pin_1, Part1.D6_PWM
  VCC: DCF_Pullup.Pin_0, SG90.vcc, Part1.5V, DCF77_Receiver_-_Conrad_1.+5V
  N9: DCF_Pullup.Pin_1, Part1.D2, DCF77_Receiver_-_Conrad_1.DCF_output
  N10: SG90.gnd, p2n2222ag.C
  N11: SG90.pulse, Part1.D9_PWM
  N12: p2n2222ag.E, Part1.GND, DCF77_Receiver_-_Conrad_1.Ground, LED1.common_cathode

custom parts:
  DCF77 641138: Low cost DCF77 receiver module. This is a radio receiver used in a radio clock, a quartz clock which is periodically set to the correct time by radio signals synchronized with an atomic clock from a government radio station. This one receives the coded time signals broadcast by German government time radio station DCF77 on 77.5 kHz. The ferrite loopstick (left) is the radio's antenna, and with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
